# Fritzing sketch IR (saved by Fritzing 0.9.0b)
breadboards: 1

parts:
  Part1 = Arduino Uno (Rev3)
  IR1 = TSOP312.., 314.. [package=THT]
  U2 = RELAY [package=relay-jzc]

nets:
  N1: Part1.D11_PWM/MOSI, IR1.Data
  N2: Part1.D2, U2.NC
  N3: Part1.5V, IR1.Vs, U2.COIL2
  GND: Part1.GND, IR1.GND, U2.NO
